// Logisim project prozessor.circ as structural Verilog: 4 circuits, main circuit main
module main (
);

  wire C, clock_1_out, clock_2_out, clock_3_out, clock_4_out, clock_5_out, clock_6_out, d_ff_1_q, d_ff_1_qn,
       EnA, EnIR, EnIX, EnPC, MuxALU, MuxMA, MuxPC, StM, Z;
  wire [1:0] alu_1_zero;
  wire [2:0] OpALU;
  wire [7:0] A_q, adder_1_out, alu_1_result, Immed, IR, IX_q, multiplexer_1_out, multiplexer_2_out,
       multiplexer_3_out, PC_q, ram_1_data;

  Adder adder_1 (.a(PC_q), .b(8'h1), .out(adder_1_out));  // open: cin, cout
  Multiplexer #(.width(8), .enable("false")) multiplexer_1 (
    .in0(adder_1_out), .in1(Immed), .out(multiplexer_1_out), .sel(MuxPC));
  // Probe on PC_q
  Register PC (.D(multiplexer_1_out), .en(EnPC), .Q(PC_q), .clk(clock_1_out));  // open: clr
  Clock clock_1 (.out(clock_1_out));
  Register A (.D(alu_1_result), .en(EnA), .Q(A_q), .clk(clock_2_out));  // open: clr
  Clock clock_2 (.out(clock_2_out));
  Multiplexer #(.width(8), .enable("false")) multiplexer_2 (
    .in0(ram_1_data), .in1(Immed), .out(multiplexer_2_out), .sel(MuxALU));
  // Probe on Immed
  ROM rom_1 (.addr(PC_q), .data(Immed), .sel(1'b1));
  // Probe on alu_1_result
  alu alu_1 (
    .A(A_q), .B(multiplexer_2_out), .Result(alu_1_result), .Carry(alu_1_zero[1]), .Zero(alu_1_zero[0]),
    .Op(OpALU));
  // Probe on IR
  Register u_IR (.D(Immed), .en(EnIR), .Q(IR), .clk(clock_3_out));  // open: clr
  Clock clock_3 (.out(clock_3_out));
  Clock clock_4 (.out(clock_4_out));
  Register #(.width(2)) register_1 (.D(alu_1_zero), .Q({C, Z}));  // open: en, clk, clr
  // Probe on multiplexer_3_out
  Register IX (.D(alu_1_result), .en(EnIX), .Q(IX_q), .clk(clock_4_out));  // open: clr
  Multiplexer #(.width(8), .enable("false")) multiplexer_3 (
    .in0(IX_q), .in1(Immed), .out(multiplexer_3_out), .sel(MuxMA));
  Clock clock_5 (.out(clock_5_out));
  Clock clock_6 (.out(clock_6_out));
  control control_1 (
    .IR(IR), .Z(Z), .C(C), .EnA(EnA), .EnIX(EnIX), .MuxALU(MuxALU), .MuxMA(MuxMA), .StM(StM), .EnPC(EnPC),
    .MuxPC(MuxPC), .EnIR(EnIR), .OpALU(OpALU), .State(d_ff_1_q));
  D_Flip_Flop d_ff_1 (.clk(clock_5_out), .D(d_ff_1_qn), .Q(d_ff_1_q), .Qn(d_ff_1_qn));  // open: preset, en, reset
  RAM #(.bus("separate")) ram_1 (
    .addr(multiplexer_3_out), .din(alu_1_result), .data(ram_1_data), .str(StM), .sel(1'b1),
    .clk(clock_6_out), .ld(1'b1));  // open: clr
  // Probe on OpALU
  // Probe on ram_1_data

  // Notes on the sheet:
  //   Program Memory
  //   Control
  //   contents of rom_1 (hex, n*v repeats v):
  //   19 5 1 a 3 20 48 3
  //   Data Path
  //   Data Memory
  //   Instruction Decoder
endmodule

module alu (
  input  [7:0] A,
  input  [7:0] B,
  input  [2:0] Op,
  output [7:0] Result,
  output Zero,
  output Carry
);

  wire adder_1_cout, subtractor_1_bout;
  wire [7:0] adder_1_out, and_1_out, or_1_out, subtractor_1_out, xor_1_out;

  Adder adder_1 (.a(A), .b(B), .out(adder_1_out), .cout(adder_1_cout));  // open: cin
  Subtractor subtractor_1 (.a(A), .b(B), .out(subtractor_1_out), .bout(subtractor_1_bout));  // open: bin
  assign and_1_out = A & B;  // AND_Gate and_1, 8 bits wide
  assign or_1_out = A | B;  // OR_Gate or_1, 8 bits wide
  assign xor_1_out = A ^ B;  // XOR_Gate xor_1, 8 bits wide
  Multiplexer #(.select(3), .width(8), .disabled(0), .enable("false")) multiplexer_1 (
    .in0(A), .in1(B), .in2(adder_1_out), .in3(subtractor_1_out), .in4(and_1_out), .in5(or_1_out),
    .in6(xor_1_out), .in7({1'b0, A[7:1]}), .out(Result), .sel(Op));
  Multiplexer #(.select(3), .disabled(0), .enable("false")) multiplexer_2 (
    .in0(1'b0), .in1(1'b0), .in2(adder_1_cout), .in3(subtractor_1_bout), .in4(1'b0), .in5(1'b0), .in6(1'b0),
    .in7(A[0]), .out(Carry), .sel(Op));
  Comparator #(.mode("unsigned")) comparator_1 (.a(Result), .b({8{1'b0}}), .eq(Zero));  // open: gt, lt
endmodule

module control (
  input  [7:0] IR,
  input  Z,
  input  C,
  input  State,
  output MuxPC,
  output EnIR,
  output EnA,
  output EnIX,
  output StM,
  output MuxMA,
  output MuxALU,
  output EnPC,
  output [2:0] OpALU
);

  wire and_1_out, and_2_out, and_3_out, control_branch_1_branch, nor_1_out, nor_2_out, not_1_out, not_2_out,
       not_3_out;

  not not_1 (not_1_out, State);
  not not_2 (not_2_out, State);
  and and_1 (and_1_out, IR[3], nor_1_out);
  nor nor_1 (nor_1_out, not_1_out, ~IR[6], IR[7]);  // NOR_Gate
  and and_2 (and_2_out, nor_1_out, control_branch_1_branch);
  control_branch control_branch_1 (
    .Branch2(IR[2]), .Branch1(IR[1]), .Branch0(IR[0]), .C(C), .Z(Z), .Branch(control_branch_1_branch));
  Decoder #(.select(2), .disabled(0)) decoder_1 (
    .out0(EnA), .out1(EnIX), .out2(StM), .sel(IR[5:4]), .en(nor_2_out));  // open: out3
  nor nor_2 (nor_2_out, not_2_out, IR[6], IR[7]);
  not not_3 (not_3_out, State);
  and and_3 (and_3_out, IR[3], State);
  or or_1 (MuxPC, and_1_out, and_2_out);
  not not_4 (EnIR, State);
  or or_2 (EnPC, not_3_out, and_3_out);

  assign MuxALU = IR[3];
  assign MuxMA = IR[3];
  assign OpALU = IR[2:0];

  // Other names for the same wires on the sheet: IParam[2:0] = IR[2:0]; IImm = IR[3]; IState = State;
  //   ITarget[1:0] = IR[5:4]; IType[1:0] = IR[7:6]
endmodule

module control_branch (
  input  Branch2,
  input  Branch1,
  input  Branch0,
  input  C,
  input  Z,
  output Branch
);

  wire and_1_out, and_2_out, and_3_out, and_4_out, and_5_out, and_6_out, and_7_out, not_1_out, not_2_out,
       not_3_out, not_4_out, not_5_out, not_6_out, not_7_out, not_8_out, not_9_out, not_10_out, not_11_out;

  not not_1 (not_1_out, Branch2);
  not not_2 (not_2_out, Branch1);
  not not_3 (not_3_out, Branch0);
  not not_4 (not_4_out, Branch2);
  not not_5 (not_5_out, Branch1);
  not not_6 (not_6_out, Z);
  not not_7 (not_7_out, Branch0);
  not not_8 (not_8_out, C);
  not not_9 (not_9_out, Branch0);
  not not_10 (not_10_out, C);
  not not_11 (not_11_out, Branch0);
  and and_1 (and_1_out, not_1_out, not_2_out, not_3_out, Z);
  and and_2 (and_2_out, not_4_out, not_5_out, Branch0, not_6_out);
  and and_3 (and_3_out, Branch1, not_7_out, C);
  and and_4 (and_4_out, Branch1, Branch0, not_8_out);
  and and_5 (and_5_out, Branch2, not_9_out, C);
  and and_6 (and_6_out, Branch2, Branch0, not_10_out);
  and and_7 (and_7_out, Branch2, Branch1, not_11_out, Z);
  or or_1 (Branch, and_1_out, and_2_out, and_3_out, and_4_out, and_5_out, and_6_out, and_7_out);
endmodule
