// Logisim project uebung_ampel.circ as structural Verilog: 3 circuits, main circuit main
module main (
  input  in_1
);

  wire ausgabefunktion_1_lampegelb, \ausgabefunktion_1_lampegrün , ausgabefunktion_1_lamperot, clock_1_out,
       d_ff_1_q, d_ff_2_q, d_ff_3_q, \zustandsübertragungsfunktion_1_z0n ,
       \zustandsübertragungsfunktion_1_z1n , \zustandsübertragungsfunktion_1_z2n ;

  \zustandsübertragungsfunktion  \zustandsübertragungsfunktion_1  (
    .M(in_1), .Z2(d_ff_1_q), .Z1(d_ff_2_q), .Z0(d_ff_3_q), .Z2n(\zustandsübertragungsfunktion_1_z2n ),
    .Z1n(\zustandsübertragungsfunktion_1_z1n ), .Z0n(\zustandsübertragungsfunktion_1_z0n ));
  Clock clock_1 (.out(clock_1_out));
  D_Flip_Flop d_ff_1 (
    .clk(clock_1_out), .D(\zustandsübertragungsfunktion_1_z2n ), .Q(d_ff_1_q));  // open: Qn, preset, en, reset
  D_Flip_Flop d_ff_2 (
    .clk(clock_1_out), .D(\zustandsübertragungsfunktion_1_z1n ), .Q(d_ff_2_q));  // open: Qn, preset, en, reset
  D_Flip_Flop d_ff_3 (
    .clk(clock_1_out), .D(\zustandsübertragungsfunktion_1_z0n ), .Q(d_ff_3_q));  // open: Qn, preset, en, reset
  ausgabefunktion ausgabefunktion_1 (
    .Z2(d_ff_1_q), .Z1(d_ff_2_q), .Z0(d_ff_3_q), .LampeRot(ausgabefunktion_1_lamperot),
    .LampeGelb(ausgabefunktion_1_lampegelb), .\LampeGrün (\ausgabefunktion_1_lampegrün ));
  LED led_1 (.in(ausgabefunktion_1_lamperot));
  LED led_2 (.in(ausgabefunktion_1_lampegelb));
  LED led_3 (.in(\ausgabefunktion_1_lampegrün ));
endmodule

module \zustandsübertragungsfunktion  (
  input  M,
  input  Z2,
  input  Z1,
  input  Z0,
  output Z2n,
  output Z1n,
  output Z0n
);

  wire and_2_out, and_3_out, and_4_out, not_1_out, not_2_out, not_3_out, not_4_out, not_5_out, not_6_out,
       not_7_out, not_8_out;

  and and_1 (Z2n, M, Z1, Z0);
  not not_1 (not_1_out, Z2);
  and and_2 (and_2_out, not_1_out, not_2_out, not_3_out);
  not not_2 (not_2_out, Z1);
  not not_3 (not_3_out, Z0);
  not not_4 (not_4_out, Z2);
  and and_3 (and_3_out, M, not_4_out, not_5_out);
  not not_5 (not_5_out, Z1);
  and and_4 (and_4_out, M, not_6_out, not_7_out);
  not not_6 (not_6_out, Z2);
  not not_7 (not_7_out, Z0);
  and and_5 (Z0n, M, not_8_out);
  not not_8 (not_8_out, Z0);
  or or_1 (Z1n, and_2_out, and_3_out, and_4_out);
endmodule

module ausgabefunktion (
  input  Z2,
  input  Z1,
  input  Z0,
  output LampeRot,
  output LampeGelb,
  output \LampeGrün 
);

  wire and_1_out, and_2_out, not_1_out, not_2_out;

  and and_1 (and_1_out, Z1, Z0);
  not not_1 (not_1_out, Z0);
  not not_2 (not_2_out, Z1);
  or or_1 (LampeRot, and_1_out, Z2);
  and and_2 (and_2_out, Z1, not_1_out);
  and and_3 (\LampeGrün , not_2_out, Z0);
  or or_2 (LampeGelb, and_2_out, Z2);
endmodule
